# Fritzing sketch research_cds_schematic (saved by Fritzing 0.9.5d)
breadboards: 1

parts:
  Mod1 = Raspberry Pi 4B
  MCP1 = MCP3208
  R4 = Resistor [tolerance=±5% resistance=10k package=THT]
  R5 = Photocell (LDR) [package=THT]

nets:
  3V3: Mod1.3V3, MCP1.VREF, MCP1.VDD, R5.pin_0
  N1: Mod1.GND, MCP1.DGND, MCP1.AGND, R4.Pin_1
  N2: Mod1.GPIO10, MCP1.DIN
  N3: Mod1.GPIO9, MCP1.DOUT
  N4: Mod1.GPIO11, MCP1.CLK
  N5: Mod1.GPIO8, MCP1.CS/SHDN
  N6: MCP1.Chan_2, R4.Pin_0, R5.pin_1
