# Fritzing sketch research_ds18b20_schematic (saved by Fritzing 0.9.5d)
breadboards: 1

parts:
  Mod1 = Raspberry Pi 4B
  DS1 = DS18B20 1-Wire Temperature Sensor [part_number=DS18B20]
  R1 = Resistor [tolerance=±5% resistance=10k package=THT]

nets:
  3V3: Mod1.3V3, DS1.VDD, R1.Pin_1
  GND: Mod1.GND, DS1.GND
  N1: Mod1.GPIO4, DS1.DQ, R1.Pin_0
