# Fritzing sketch research_scd41_schematic (saved by Fritzing 0.9.5d)
breadboards: 1

parts:
  Mod1 = Raspberry Pi 4B
  パーツ1 = Adafruit SCD4x [part_number="Adafruit #5187"]

nets:
  3V3: Mod1.3V3, パーツ1.VCC
  N1: Mod1.GPIO2, パーツ1.SCL
  N2: Mod1.GPIO3, パーツ1.SDA
  GND: Mod1.GND, パーツ1.GND

custom parts:
  Adafruit SCD4x: Take a deep breath in...now slowly breathe out. Mmm isn't it wonderful? All that air around us, which we bring into our lungs, extracts oxygen from and then breathes out carbon dioxide. CO2 is essential for life on this planet we call Earth - we and plants take turns using and emitting CO2 in an elegant symbiosis. But it's important to keep that CO2 balanced - you don't want too much around,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
