# Fritzing sketch research_sensors_schematic (saved by Fritzing 0.9.5d)
breadboards: 1

parts:
  Mod1 = Raspberry Pi 4B
  DS1 = DS18B20 1-Wire Temperature Sensor [part_number=DS18B20]
  S1 = Pushbutton [package=THT]
  S2 = Pushbutton [package="[THT]"]
  R2 = Resistor [tolerance=±5% resistance=330 package=THT]
  LED1 = LED - 3mm [color="Red (633nm)" package="3 mm [THT]"]
  パーツ1 = Adafruit SCD4x [part_number="Adafruit #5187"]
  R1 = Resistor [tolerance=±5% resistance=10k package=THT]

nets:
  3V3: Mod1.3V3, DS1.VDD, S1.leg1, S2.Pin_3, S2.Pin_4, パーツ1.VCC, R1.Pin_1
  N1: Mod1.GPIO2, パーツ1.SCL
  N2: Mod1.GPIO3, パーツ1.SDA
  GND: Mod1.GND, DS1.GND, LED1.cathode, パーツ1.GND
  N3: Mod1.GPIO4, DS1.DQ, R1.Pin_0
  N4: Mod1.GPIO16, R2.Pin_0
  N5: Mod1.GPIO20, S2.Pin_1, S2.Pin_2
  N6: Mod1.GPIO21, S1.leg0
  N7: R2.Pin_1, LED1.anode

custom parts:
  Adafruit SCD4x: Take a deep breath in...now slowly breathe out. Mmm isn't it wonderful? All that air around us, which we bring into our lungs, extracts oxygen from and then breathes out carbon dioxide. CO2 is essential for life on this planet we call Earth - we and plants take turns using and emitting CO2 in an elegant symbiosis. But it's important to keep that CO2 balanced - you don't want too much around,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
